# Fritzing sketch Esquema_SIN_reguladores (saved by Fritzing 0.9.3b)

parts:
  M1 = DOIT Esp32 DevKit v1 (30 pins long, 11 pins width) [part_number=ESP32S-PIN30]
  J1 = Basic Servo
  J2 = Basic Servo
  Power_plug1 = Power plug
  U4 = WS2812 RGB LED strip

nets:
  GND: M1.GND, Power_plug1.GND
  N1: M1.D4, J2.pulse
  N2: M1.D5, U4.DIN
  N3: M1.D18, J1.pulse
  VIN: M1.VIN, Power_plug1.VCC
  GND_2: J1.gnd, J2.gnd
  VCC: J1.vcc, J2.vcc

notes:
  5v

custom parts:
  DOIT Esp32 DevKit v1 (30 pins long, 11 pins width): The DOIT Esp32 DevKit v1 is one of the development board created by DOIT to evaluate the ESP-WROOM-32 module. It is based on the ESP32 microcontroller that boasts Wifi, Bluetooth, Ethernet and Low Power support all in a single chip. (vanepp) made breadboard work, adjusted pin numbering and labels and reduced size of schematic and cleaned up pcb. This chip is 30pins long (2 x15) and 11 pins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
  WS2812 RGB LED strip: WS2812 strip
